// Logisim project stargate323_LogisimEvolution.circ as structural Verilog: 1 circuit, main circuit main
module main (
);

  wire and_1_out, and_2_out, and_3_out, and_4_out, and_5_out, and_6_out, and_7_out, and_8_out, and_9_out,
       and_10_out, and_11_out, and_12_out, and_13_out, and_14_out, and_15_out, and_16_out, and_17_out,
       buffer_1_out, CAS, clk_out, DAC, DACEN, DECAY_p1, DECAY_p2, DECAY_p3, dipswitch_1_p1, dipswitch_1_p2,
       ISH, LSBE, MCCK, MSBE, n7474_1_pin9, n7474_1_pin10, n7474_1_pin13, n7474_2_pin9, n7474_2_pin10,
       n7474_2_pin12, n7485_1_pin2, n7485_1_pin3, n7485_1_pin4, n7485_1_pin7, n7485_2_pin2, n7485_2_pin3,
       n7485_2_pin4, n7485_2_pin9, nand_1_out, nand_2_out, nand_3_out, nand_4_out, nDAC, nDACX, nEF, nEL,
       nER, nET, nGSN, nMOD, nor_1_out, nor_2_out, nor_3_out, nor_4_out, nor_5_out, nor_6_out, nor_7_out,
       nor_8_out, not_12_out, not_14_out, not_15_out, not_16_out, not_19_out, not_22_out, not_23_out,
       not_24_out, not_25_out, not_26_out, not_27_out, not_28_out, not_29_out, not_30_out, not_31_out,
       not_32_out, nS, nSYNCCLEAR, nTCB1, nTCB7, P0, P1, P2, PD0, PD1, PD2, PD3, PREDELAY_p1, PREDELAY_p2,
       PREDELAY_p3, PREDELAY_p4, PROGRAM_p1, PROGRAM_p2, PROGRAM_p3, RAS, RD0, RD1, RD2, RESET_out, RL0, RL1,
       RL2, RL3, SARCK, TCB2, U52_pin1, U52_pin3, U52_pin4, U52_pin5, U52_pin6, U52_pin7, U52_pin9, U53_pin1,
       U53_pin3, U53_pin4, U53_pin5, U53_pin6, U53_pin7, U53_pin9, U53_pin10, U57_pin1, U57_pin4, U70_pin7,
       U72_pin3, U72_pin4, U72_pin5, U72_pin6, U72_pin7, U72_pin9, U73_pin3, U73_pin4, U73_pin5, U73_pin6,
       U73_pin7, U73_pin9, U73_pin10, U75_pin1, U75_pin7, U75_pin9, U75_pin10, U75_pin15;
  wire [5:0] register_2_q;
  wire [5:1] TCB2_7;
  wire [6:0] G1_7;
  wire [7:0] ADDRESS, BITTIME, COL, DD0_7, GAIN, GM0_7, multiplexer_1_out, multiplexer_5_out, not_20_out,
       not_21_out, P0803_data, P0804_data, P0805_data, P0806_data, P0807_data, P0808_data, P0810_data,
       P0811_data, register_1_q, ROW, WR0_7;
  wire [12:0] MC0_12;

  // DipSwitch #(.number(3)) PROGRAM: pin names not known; wires that end beside it: PROGRAM_p1, PROGRAM_p2, PROGRAM_p3
  not not_1 (P2, PROGRAM_p3);
  not not_2 (P1, PROGRAM_p2);
  not not_3 (P0, PROGRAM_p1);
  // DipSwitch #(.number(4)) PREDELAY: pin names not known; wires that end beside it: PREDELAY_p1, PREDELAY_p2, PREDELAY_p3, PREDELAY_p4
  not not_4 (PD3, PREDELAY_p4);
  not not_5 (PD2, PREDELAY_p3);
  not not_6 (PD1, PREDELAY_p2);
  not not_7 (PD0, PREDELAY_p1);
  Register register_1 (.D(ADDRESS), .clk(RAS), .Q(register_1_q));  // open: en, clr
  Register #(.width(6)) register_2 (.D(ADDRESS[6:1]), .clk(CAS), .Q(register_2_q));  // open: en, clr
  // DipSwitch #(.number(3)) DECAY: pin names not known; wires that end beside it: DECAY_p1, DECAY_p2, DECAY_p3
  not not_8 (RD2, DECAY_p3);
  not not_9 (RD1, DECAY_p2);
  not not_10 (RD0, DECAY_p1);
  // Probe on TCB2_7[5]
  // Probe on ROW
  // Probe on BITTIME
  // Probe on GAIN
  // Probe on register_1_q
  // Probe on register_2_q
  // DipSwitch #(.number(4)) RATLVL: pin names not known; wires that end beside it: RL0, RL1, RL2, RL3
  and and_1 (and_1_out, COL[1], dipswitch_1_p1);
  // DipSwitch #(.number(2)) dipswitch_1: pin names not known; wires that end beside it: dipswitch_1_p1, dipswitch_1_p2
  // NOT_Gate not_11 has open pins: in=and_1_out, out=open
  Clock #(.highDuration(4), .lowDuration(4)) clk (.out(clk_out));
  Clock sysclk (.out(dipswitch_1_p2));
  _74163 #(.ShowInternalStructure("true")) U52 (
    .pin1(U52_pin1), .pin2(clk_out), .pin3(U52_pin3), .pin4(U52_pin4), .pin5(U52_pin5), .pin6(U52_pin6),
    .pin7(U52_pin7), .pin14(BITTIME[4]), .pin13(BITTIME[5]), .pin12(BITTIME[6]), .pin11(BITTIME[7]),
    .pin10(U52_pin7), .pin9(U52_pin9));  // open: pin15
  _74163 #(.ShowInternalStructure("true")) U53 (
    .pin1(U53_pin1), .pin2(clk_out), .pin3(U53_pin3), .pin4(U53_pin4), .pin5(U53_pin5), .pin6(U53_pin6),
    .pin7(U53_pin7), .pin15(U52_pin7), .pin14(BITTIME[0]), .pin13(BITTIME[1]), .pin12(BITTIME[2]),
    .pin11(BITTIME[3]), .pin10(U53_pin10), .pin9(U53_pin9));
  ROM P0810 (.addr(BITTIME), .data(P0810_data));
  ROM P0811 (.addr(BITTIME), .data(P0811_data));
  not not_12 (not_12_out, BITTIME[1]);
  D_Flip_Flop d_ff_1 (.D(not_12_out), .clk(clk_out), .Q(nTCB1));  // open: Qn, preset, reset
  D_Flip_Flop d_ff_2 (.D(P0810_data[7]), .clk(clk_out), .Q(nMOD));  // open: Qn, preset, reset
  D_Flip_Flop d_ff_3 (.D(P0810_data[6]), .clk(clk_out), .Q(nS));  // open: Qn, preset, reset
  D_Flip_Flop d_ff_4 (.D(P0810_data[5]), .clk(clk_out), .Q(SARCK));  // open: Qn, preset, reset
  D_Flip_Flop d_ff_5 (.D(P0810_data[4]), .clk(clk_out), .Q(RAS));  // open: Qn, preset, reset
  D_Flip_Flop d_ff_6 (.D(P0810_data[3]), .clk(clk_out), .Q(CAS));  // open: Qn, preset, reset
  D_Flip_Flop d_ff_7 (.D(P0810_data[2]), .clk(clk_out), .Q(DACEN));  // open: Qn, preset, reset
  D_Flip_Flop d_ff_8 (.D(P0810_data[1]), .clk(clk_out), .Q(DAC));  // open: Qn, preset, reset
  D_Flip_Flop d_ff_9 (.D(P0811_data[7]), .clk(clk_out), .Q(LSBE));  // open: Qn, preset, reset
  D_Flip_Flop d_ff_10 (.D(P0811_data[6]), .clk(clk_out), .Q(MSBE));  // open: Qn, preset, reset
  D_Flip_Flop d_ff_11 (.D(P0811_data[5]), .clk(clk_out), .Q(nET));  // open: Qn, preset, reset
  D_Flip_Flop d_ff_12 (.D(P0811_data[4]), .clk(clk_out), .Q(nEF));  // open: Qn, preset, reset
  D_Flip_Flop d_ff_13 (.D(P0811_data[3]), .clk(clk_out), .Q(nEL));  // open: Qn, preset, reset
  D_Flip_Flop d_ff_14 (.D(P0811_data[2]), .clk(clk_out), .Q(nER));  // open: Qn, preset, reset
  D_Flip_Flop d_ff_15 (.D(P0811_data[1]), .clk(clk_out), .Q(ISH));  // open: Qn, preset, reset
  D_Flip_Flop d_ff_16 (.D(P0811_data[0]), .clk(clk_out), .Q(nDACX));  // open: Qn, preset, reset
  D_Flip_Flop d_ff_17 (.D(P0810_data[0]), .clk(clk_out), .Q(nSYNCCLEAR));  // open: Qn, preset, reset
  not not_13 (nDAC, DAC);
  not not_14 (not_14_out, nTCB1);
  ROM P0803 (.addr({1'b0, P2, P1, P0, RL3, RL2, RL1, RL0}), .data(P0803_data));
  not not_15 (not_15_out, not_14_out);
  Counter #(.max('h1fff), .trigger("falling"), .width(13)) U87_U88 (
    .up(1'b1), .count(1'b1), .clk(not_16_out), .Q(MC0_12));  // open: clr, load, D, carry
  not not_16 (not_16_out, MCCK);
  _74163 #(.ShowInternalStructure("true")) U72 (
    .pin1(nSYNCCLEAR), .pin2(not_15_out), .pin3(U72_pin3), .pin4(U72_pin4), .pin5(U72_pin5), .pin6(U72_pin6),
    .pin7(U72_pin7), .pin14(TCB2_7[4]), .pin13(TCB2_7[5]), .pin10(U72_pin7), .pin9(U72_pin9));  // open: pin15, pin12, pin11
  _74163 #(.ShowInternalStructure("true")) U73 (
    .pin1(nSYNCCLEAR), .pin2(not_15_out), .pin3(U73_pin3), .pin4(U73_pin4), .pin5(U73_pin5), .pin6(U73_pin6),
    .pin7(U73_pin7), .pin15(U72_pin7), .pin14(TCB2), .pin13(TCB2_7[1]), .pin12(TCB2_7[2]), .pin11(TCB2_7[3]),
    .pin10(U73_pin10), .pin9(U73_pin9));
  not not_17 (nTCB7, TCB2_7[5]);
  _74161 #(.ShowInternalStructure("true")) U75 (
    .pin1(U75_pin1), .pin2(TCB2_7[5]), .pin3(P0803_data[0]), .pin4(P0803_data[1]), .pin5(P0803_data[2]),
    .pin6(P0803_data[3]), .pin7(U75_pin7), .pin15(U75_pin15), .pin10(U75_pin10), .pin9(U75_pin9));  // open: pin14, pin13, pin12, pin11
  _7474 #(.ShowInternalStructure("true")) U57 (
    .pin1(U57_pin1), .pin2(U75_pin15), .pin3(nTCB7), .pin4(U57_pin4), .pin5(MCCK));  // open: pin6, pin13, pin12, pin11, pin10, pin9, pin8
  not not_18 (U75_pin9, U75_pin15);
  ROM #(.addrWidth(12)) P0804 (.addr({MC0_12[12:6], TCB2_7}), .data(P0804_data));
  Button RESET (.out(RESET_out));
  Counter #(.trigger("falling")) U82 (
    .clr(RESET_out), .up(1'b1), .count(1'b1), .clk(ROW[7]), .Q(COL));  // open: load, D, carry
  Counter #(.trigger("falling")) U85 (
    .clr(RESET_out), .up(1'b1), .count(1'b1), .clk(not_19_out), .Q(ROW));  // open: load, D, carry
  not not_19 (not_19_out, nTCB7);
  ROM #(.addrWidth(12)) P0807 (.addr({MC0_12[12:6], TCB2_7}), .data(P0807_data));
  Multiplexer #(.width(8)) multiplexer_1 (.in0(P0804_data), .in1({8{1'b0}}), .out(multiplexer_1_out), .sel(nDAC));
  Pull_Resistor #(.pull(1)) pull_resistor_1 (.node(multiplexer_1_out[3]));
  ROM #(.addrWidth(11)) P0806 (.addr({P2, P1, P0, RD2, RD1, RD0, TCB2_7}), .data(P0806_data));
  nand nand_1 (nand_1_out, nTCB1, nTCB1);
  ROM #(.addrWidth(12)) P0805 (.addr({MC0_12[8:0], multiplexer_1_out[2:0]}), .data(P0805_data));
  _7474 #(.ShowInternalStructure("true")) u_7474_1 (
    .pin13(n7474_1_pin13), .pin12(TCB2), .pin11(nand_1_out), .pin10(n7474_1_pin10), .pin9(n7474_1_pin9));  // open: pin1, pin2, pin3, pin4, pin5, pin6, pin8
  assign not_20_out = ~ROW;  // NOT_Gate not_20, 8 bits wide
  assign not_21_out = ~COL;  // NOT_Gate not_21, 8 bits wide
  Multiplexer #(.width(8)) multiplexer_2 (.in0(not_20_out), .in1(not_21_out), .out(WR0_7), .sel(TCB2));
  nand nand_2 (nand_2_out, n7474_1_pin9, nTCB1);
  Multiplexer #(.width(8)) multiplexer_3 (
    .in0(P0806_data), .in1({8{1'b0}}),
    .out({nGSN, G1_7[0], G1_7[1], G1_7[2], G1_7[3], G1_7[4], G1_7[5], G1_7[6]}), .sel(nDACX));
  Multiplexer #(.width(8)) multiplexer_4 (.in0(P0805_data), .in1({8{1'b0}}), .out(GM0_7), .sel(multiplexer_1_out[3]));
  ROM #(.addrWidth(13)) P0808 (.addr({PD3, P2, P1, P0, PD2, PD1, PD0, TCB2_7, TCB2}), .data(P0808_data));
  _7485 #(.ShowInternalStructure("true")) u_7485_1 (
    .pin1(G1_7[6]), .pin2(n7485_1_pin2), .pin3(n7485_1_pin3), .pin4(n7485_1_pin4), .pin7(n7485_1_pin7),
    .pin15(GM0_7[7]), .pin14(G1_7[5]), .pin13(GM0_7[6]), .pin12(GM0_7[5]), .pin11(G1_7[4]), .pin10(GM0_7[4]),
    .pin9(G1_7[3]));  // open: pin5, pin6
  _7485 #(.ShowInternalStructure("true")) u_7485_2 (
    .pin1(G1_7[2]), .pin2(n7485_2_pin2), .pin3(n7485_2_pin3), .pin4(n7485_2_pin4), .pin5(n7485_1_pin4),
    .pin6(n7485_1_pin3), .pin7(n7485_1_pin2), .pin15(GM0_7[3]), .pin14(G1_7[1]), .pin13(GM0_7[2]),
    .pin12(GM0_7[1]), .pin11(G1_7[0]), .pin10(GM0_7[0]), .pin9(n7485_2_pin9));
  nand nand_3 (nand_3_out, multiplexer_1_out[3], 1'b1);
  // Probe on P0808_data
  not not_22 (not_22_out, nMOD);
  nand nand_4 (nand_4_out, nand_3_out, n7485_1_pin7);
  _7474 #(.ShowInternalStructure("true")) u_7474_2 (
    .pin13(RAS), .pin12(n7474_2_pin12), .pin11(nTCB1), .pin10(n7474_2_pin10), .pin9(n7474_2_pin9));  // open: pin1, pin2, pin3, pin4, pin5, pin6, pin8
  Multiplexer #(.width(8)) multiplexer_5 (
    .in0(P0808_data), .in1(P0807_data), .out(multiplexer_5_out), .sel(not_22_out));
  // Probe on not_22_out
  _74283 #(.ShowInternalStructure("true")) U70 (
    .pin1(ADDRESS[6]), .pin2(DD0_7[5]), .pin3(WR0_7[5]), .pin4(ADDRESS[5]), .pin5(WR0_7[4]), .pin6(DD0_7[4]),
    .pin7(U70_pin7), .pin15(DD0_7[6]), .pin14(WR0_7[6]), .pin13(ADDRESS[0]), .pin12(WR0_7[7]),
    .pin11(DD0_7[7]), .pin10(ADDRESS[7]), .pin9(n7474_2_pin12));
  _74283 #(.ShowInternalStructure("true")) U63 (
    .pin1(ADDRESS[2]), .pin2(DD0_7[1]), .pin3(WR0_7[1]), .pin4(ADDRESS[1]), .pin5(WR0_7[0]), .pin6(DD0_7[0]),
    .pin7(n7474_2_pin9), .pin15(DD0_7[2]), .pin14(WR0_7[2]), .pin13(ADDRESS[3]), .pin12(WR0_7[3]),
    .pin11(DD0_7[3]), .pin10(ADDRESS[4]), .pin9(U70_pin7));
  // Probe on multiplexer_5_out
  not not_23 (not_23_out, nand_4_out);
  not not_24 (not_24_out, not_23_out);
  Register U62 (.D(multiplexer_5_out), .en(1'b1), .clk(nTCB1), .Q(DD0_7));  // open: clr
  and and_2 (and_2_out, GM0_7[7], not_23_out);
  and and_3 (and_3_out, not_24_out, G1_7[0]);
  and and_4 (and_4_out, GM0_7[6], not_23_out);
  and and_5 (and_5_out, not_24_out, G1_7[1]);
  and and_6 (and_6_out, GM0_7[5], not_23_out);
  and and_7 (and_7_out, not_24_out, G1_7[2]);
  and and_8 (and_8_out, GM0_7[4], not_23_out);
  and and_9 (and_9_out, not_24_out, G1_7[3]);
  and and_10 (and_10_out, GM0_7[3], not_23_out);
  and and_11 (and_11_out, not_24_out, G1_7[4]);
  and and_12 (and_12_out, GM0_7[2], not_23_out);
  and and_13 (and_13_out, not_24_out, G1_7[5]);
  and and_14 (and_14_out, GM0_7[1], not_23_out);
  and and_15 (and_15_out, not_24_out, G1_7[6]);
  and and_16 (and_16_out, GM0_7[0], not_23_out);
  and and_17 (and_17_out, not_24_out, 1'b0);
  buf buffer_1 (buffer_1_out, nand_2_out);
  nor nor_1 (nor_1_out, and_2_out, and_3_out);
  not not_25 (not_25_out, nor_1_out);
  nor nor_2 (nor_2_out, and_4_out, and_5_out);
  not not_26 (not_26_out, nor_2_out);
  nor nor_3 (nor_3_out, and_6_out, and_7_out);
  not not_27 (not_27_out, nor_3_out);
  nor nor_4 (nor_4_out, and_8_out, and_9_out);
  not not_28 (not_28_out, nor_4_out);
  nor nor_5 (nor_5_out, and_10_out, and_11_out);
  not not_29 (not_29_out, nor_5_out);
  nor nor_6 (nor_6_out, and_12_out, and_13_out);
  not not_30 (not_30_out, nor_6_out);
  nor nor_7 (nor_7_out, and_14_out, and_15_out);
  not not_31 (not_31_out, nor_7_out);
  nor nor_8 (nor_8_out, and_16_out, and_17_out);
  not not_32 (not_32_out, nor_8_out);
  S_R_Flip_Flop s_r_ff_1 (.S(not_25_out), .R(nor_1_out), .clk(buffer_1_out), .Q(GAIN[7]));  // open: reset, Qn, preset
  S_R_Flip_Flop s_r_ff_2 (.S(not_26_out), .R(nor_2_out), .clk(buffer_1_out), .Q(GAIN[6]));  // open: reset, Qn, preset
  S_R_Flip_Flop s_r_ff_3 (.S(not_27_out), .R(nor_3_out), .clk(buffer_1_out), .Q(GAIN[5]));  // open: reset, Qn, preset
  S_R_Flip_Flop s_r_ff_4 (.S(not_28_out), .R(nor_4_out), .clk(buffer_1_out), .Q(GAIN[4]));  // open: reset, Qn, preset
  S_R_Flip_Flop s_r_ff_5 (.S(not_29_out), .R(nor_5_out), .clk(buffer_1_out), .Q(GAIN[3]));  // open: reset, Qn, preset
  S_R_Flip_Flop s_r_ff_6 (.S(not_30_out), .R(nor_6_out), .clk(buffer_1_out), .Q(GAIN[2]));  // open: reset, Qn, preset
  S_R_Flip_Flop s_r_ff_7 (.S(not_31_out), .R(nor_7_out), .clk(buffer_1_out), .Q(GAIN[1]));  // open: reset, Qn, preset
  S_R_Flip_Flop s_r_ff_8 (.S(not_32_out), .R(nor_8_out), .clk(buffer_1_out), .Q(GAIN[0]));  // open: reset, Qn, preset
  // also tied to GND on the sheet: {U52_pin3, U52_pin4, U52_pin5, U52_pin6, U53_pin3, U53_pin4, U53_pin5, U53_pin6, U72_pin3, U72_pin4, U72_pin5, U72_pin6, U73_pin3, U73_pin4, U73_pin5, U73_pin6, n7485_2_pin9, n7485_2_pin4, n7485_2_pin2}
  // also tied to VCC on the sheet: {U52_pin1, U53_pin1, U53_pin7, U52_pin9, U53_pin10, U53_pin9, U73_pin7, U72_pin9, U73_pin10, U73_pin9, U75_pin1, U75_pin7, U75_pin10, U57_pin1, U57_pin4, n7474_1_pin13, n7474_1_pin10, n7485_2_pin3, n7474_2_pin10}

  // Other names for the same wires on the sheet: TCB2_7[0] = TCB2; TCB3 = TCB2_7[1]; TCB4 = TCB2_7[2];
  //   TCB5 = TCB2_7[3]; TCB6 = TCB2_7[4]; TCB7 = TCB2_7[5]; PAUSE = COL[1]

  // Notes on the sheet:
  //   contents of P0810 (hex, n*v repeats v):
  //   e4 e4 e4 e5 e5 c5 5*e5 c5 4*e5 c5 e5 e5 e5 c5 e5 e5 e5 c5 e5 e5 c5 e5 e5 c5 e5 85 a5 e5 e5 e5 c5 e5
  //   e5 e5 c5 e5 e5 e5 c5 e5 e5 e5 c5 e5 e5 c5 e5 e5 c5 e5 e5 d5 f5 75 55 75 7d fb 9b a3 f3 73 73 7b 7b
  //   ff fb e3 f3 73 73 7b 7b ff fb e3 f3 73 73 7b 7b ff fb e3 f3 73 73 7b 7b ff fb e3 f3 73 73 7b 7b ff
  //   fb e3 f3 73 73 7b 7b ff fb e3 f3 73 73 7b 7b ff fb e3 f3 73 73 7b 7b ff fb e3 f3 73 73 7b 7b ff fb
  //   e3 f3 73 73 7b 7b ff fb e3 f3 73 73 7b 7b ff fb e3 f3 73 73 7b 7b ff fb e3 f3 73 73 7b 7b ff fb e3
  //   f3 73 73 7b 7b ff fb e3 f3 f3 f3 fb fb ff fb e3 f3 f3 f3 fb fb ff fb e3 f3 f3 f3 fb fb ff fb e3 f3
  //   f3 f3 fb fb ff fb e3 f3 f3 f3 fb fb ff fb e3 f3 f3 f3 fb fb ff fb e3 f3 f3 f3 fb fb ff fb e3 f3 f3
  //   f3 fb fb ff fb e3 f3 f3 f3 fb fb ff fb e3 e3 eb e2 c2 e2
  //   contents of P0811 (hex, n*v repeats v):
  //   32*7d 24*bd 8*bc 4*3e 4*1e 4*3e 4*2e 4*3e 4*2e 4*3e 4*2e 4*3e 4*2e 4*3e 4*2e 4*3e 4*2e 4*3e 4*2e
  //   4*3e 4*2e 4*3e 4*2e 4*3e 4*2e 4*3e 4*2e 4*3e 4*2e 4*3e 4*2e 4*3e 4*2e 4*3e 4*2e 4*3e 4*36 4*3e 4*36
  //   3e 3c 3c 3c 4*34 4*3c 4*34 4*3c 4*38 4*3c 4*38 4*3c 4*38 4*3d 4*39
  //   contents of P0803 (hex, n*v repeats v):
  //   eb ea e9 e9 12*e7 eb e9 e7 e7 12*e5 ec eb 14*ea 4*ec 13*ea e8 e6 e6 12*e4 ea e9 e7 e7 12*e4 e9 e7 e5
  //   e5 12*e4 e9 e6 e5 e5 12*e4 eb ea e9 e9 12*e7 eb e9 e7 e7 12*e5 ec eb 14*ea 4*ec 13*ea e8 e6 e6 12*e4
  //   ea e9 e7 e7 12*e4 e9 e7 e5 e5 12*e4 e9 e6 e5 e5 12*e4
  //   contents of P0804 (hex, n*v repeats v):
  //   8*ff cf d5 d3 c4 df c7 c3 d5 c1 c4 d7 c1 c0 c0 d2 17*ff cf c5 d3 c4 d1 c7 c3 c5 c1 c4 d7 cf c0 c0 d2
  //   17*ff c2 c5 d3 c4 d1 c7 c3 c5 c1 c4 d7 cf c0 c0 d2 17*ff c2 c5 df c4 d1 d7 c3 c5 c1 c4 c7 cf c0 c0
  //   d2 17*ff c2 c5 df cf d1 d7 c3 c5 c1 c4 c7 c4 d0 d0 d2 17*ff c2 c5 d5 cf c1 d7 c3 cf d1 c4 c7 c4 d0
  //   d0 d2 17*ff d2 c5 d5 c6 c1 d7 c3 cf d1 c4 c7 c4 d0 d0 c2 17*ff d2 c5 d5 c6 c1 df d3 c7 d1 c4 cf c4
  //   d0 d0 c2 17*ff d2 c5 d5 c6 c1 d0 d3 c7 d1 d4 cf d4 df d0 c2 17*ff d2 d5 c5 c6 c1 d0 d3 c7 df d4 cf
  //   d4 df d0 c2 17*ff d2 d5 c5 d6 c1 d0 d3 c7 df d4 c2 d4 df d0 cf 17*ff d2 d5 c5 d6 c1 d0 df d7 df d4
  //   c2 d4 d3 d0 cf 17*ff d2 d5 c5 d6 c1 c0 df d7 d4 df c2 d4 d3 c0 cf 17*ff d2 df c5 d6 d1 c0 d5 d7 d4
  //   df c2 d4 d3 c0 cf 17*ff c2 df c5 df d1 c0 d5 d7 d4 df d2 d4 d3 c0 c6 17*ff c2 df c5 df d1 c0 d5 df
  //   d4 d7 d2 d4 c3 c0 c6 17*ff c2 df c5 d0 d1 cf d5 df c4 d7 d2 c4 c3 cf c6 17*ff c2 d1 d5 d0 df c1 c5
  //   df c4 d7 d2 c4 c3 cf c6 17*ff cf d1 d5 d0 df c1 c5 d2 c4 d7 df c4 c3 cf d6 17*ff cf d1 d5 d0 df c1
  //   c5 d2 c4 c7 df c4 cf c3 d6 17*ff cf d1 d5 c0 d4 c1 c5 d2 cf c7 d4 cf cf c3 d6 17*ff c5 c1 df c0 d4
  //   d1 cf d2 cf c7 d4 cf c5 c3 d6 17*ff c5 c1 df c0 d4 d1 cf c2 c6 c7 d4 c6 c5 c3 df 17*ff c5 c1 d7 c0
  //   d4 d1 c7 c2 c6 cf d4 c6 c5 d3 df 17*ff c5 c1 d7 cf c4 d1 c7 c2 c6 cf c4 c6 c5 d3 d0 17*ff d5 cf d7
  //   c1 c4 df c7 c2 c6 c1 c4 c6 d5 d3 d0 17*ff d5 cf d7 c1 c4 df c7 c2 d6 c1 c4 d6 d5 d3 d0 17*ff d5 c3
  //   c7 c1 c4 df d7 c2 d6 c1 c4 d6 d5 df d0 17*ff d5 c3 c7 c1 cf d4 d7 c2 d6 c1 c4 d6 d5 df c0 17*ff df
  //   c3 c7 d1 cf d4 d7 c2 d6 d1 c4 d6 df d5 c0 17*ff df c3 c7 d1 c6 d4 d7 d2 df d1 c4 df d6 d5 c0 17*ff
  //   d7 d3 cf d1 c6 d4 d7 d2 df d1 c4 df d6 d5 c0 17*ff d7 d3 cf d1 c6 c4 d7 d2 d0 d1 d4 d0 d6 d5 cf
  //   17*ff d7 d3 c1 df c6 c4 d7 d2 d0 df d4 d0 d6 c5 cf 17*ff d7 d3 c1 d2 d6 c4 d7 df d0 df d4 d0 c6 c5
  //   c2 17*ff c7 df c1 d2 d6 c4 c7 df d0 d3 d4 d0 c6 c5 c2 17*ff c7 df c1 d2 d6 cf c7 d4 c0 d3 df c0 c6
  //   c5 c2 17*ff c7 d5 d1 d2 d6 cf c7 d4 c0 d3 df c0 c6 cf c2 17*ff c7 d5 d1 c2 df c6 c7 d4 c0 d3 df c0
  //   cf c6 d2 17*ff cf d5 d1 c2 df c6 cf d4 c0 c3 df c0 cf c6 d2 17*ff cf d5 d1 c2 d0 c6 cf c4 cf c3 d0
  //   cf cf c6 d2 17*ff c1 c5 df c2 d0 c6 cf c4 cf c3 d0 cf c1 c6 d2 17*ff c1 c5 df cf d0 d6 cf c4 c2 c3
  //   d0 c2 c1 d6 df 17*ff c1 c5 d3 cf d0 d6 c3 c4 c2 cf d0 c2 c1 d6 df 17*ff c1 c5 d3 cf c0 d6 c3 cf c2
  //   cf c0 c2 c1 d6 d4 17*ff d1 cf d3 c5 c0 d6 c3 cf c2 c5 c0 c2 d1 d6 d4 17*ff d1 cf d3 c5 c0 d6 c3 c6
  //   d2 c5 c0 d2 d1 df d4 17*ff d1 c7 c3 c5 c0 d6 d3 c6 d2 c5 c0 d2 d1 df d4 17*ff d1 c7 c3 c5 cf d6 d3
  //   c6 d2 c5 cf d2 d1 d0 c4 17*ff df c7 c3 d5 c1 d6 d3 c6 d2 d5 cf d2 d1 d0 c4 17*ff d2 c7 c3 d5 c1 c6
  //   d3 d6 df d5 c2 df d1 d0 c4 17*ff d2 d7 cf d5 c1 c6 d3 d6 df d5 c2 df d1 d0 c4 17*ff d2 d7 cf d5 c1
  //   c6 d3 d6 d4 d5 c2 d4 d1 c0 cf 17*ff d2 d7 c5 df d1 c6 d3 d6 d4 df c2 d4 c1 c0 c5 17*ff c2 d7 c5 df
  //   d1 cf d3 df d4 d6 d2 d4 c1 c0 c5 17*ff c2 df c5 d7 d1 cf c3 df d4 d6 d2 d4 c1 c0 c5 17*ff c2 df c5
  //   d7 d1 cf c3 d0 c4 d6 d2 c4 c1 cf c5 17*ff c2 d1 d5 d7 df cf c3 d0 c4 d6 d2 c4 cf cf d5 17*ff cf d1
  //   d5 d7 df c2 c3 d0 c4 c6 df c4 cf cf d5 17*ff cf d1 d5 c7 df c2 cf d0 c4 c6 d3 c4 cf c3 d5 17*ff cf
  //   d1 d5 c7 d4 c2 cf c0 cf c6 d3 cf c4 c3 d5 17*ff c5 c1 df c7 d4 c2 cf c0 c5 c6 d3 cf c4 c3 df 17*ff
  //   c5 c1 df c7 d4 d2 c6 c0 c5 cf d3 c6 c4 c3 df 17*ff c5 c1 d7 cf d4 d2 c6 c0 c5 cf c3 c6 c4 d3 d7
  //   17*ff c5 c1 d7 cf c4 d2 c6 cf c5 c0 c3 c6 d4 d3 d7 17*ff d5 cf d7 c1 c4 d2 c6 cf d5 c0 c3 c6 d4 d3
  //   d7 17*ff d5 cf d7 c1 c4 df d6 c2 d5 c0 c3 d6 d4 d3 d7 17*ff d5 c3 c7 c1 c4 d3 d6 c2 d5 c0 cf d6 d4
  //   df c7 17*ff d5 c3 c7 c1 cf d3 d6 c2 d5 d0 cf d6 df df c7 17*ff df c3 c7 d1 cf d3 d6 c2 df d0 c5 d6
  //   df d5 c7 17*ff d6 c3 c7 d1 c6 d3 df d2 df d0 c5 df df d5 c7 17*ff d6 d3 cf d1 c6 c3 df d2 df d0 c5
  //   d7 d7 d5 cf 17*ff d6 d3 c0 d1 c6 c3 df d2 d0 df c5 d7 d7 d5 cf 17*ff d6 d3 c0 df c6 c3 d1 d2 d0 df
  //   d5 d7 d7 c5 cf 17*ff c6 d3 c0 df d6 c3 d1 df d0 df d5 d7 d7 c5 c2 17*ff c6 df c0 d3 d6 cf d1 df d0
  //   d3 d5 c7 c7 c5 c2 17*ff c6 d4 d0 d3 d6 cf d1 d4 c0 d3 d5 c7 c7 c5 c2 17*ff c6 d4 d0 d3 d6 cf c1 d4
  //   c0 d3 df c7 c7 cf c2 17*ff cf d4 d0 d3 df c6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
  //   contents of P0807 (hex, n*v repeats v):
  //   6*ff 2e ed a9 5c 35 ef 4 ac 72 a6 3c ad 1e ed ae e5 16*ff 2e ed 8e 5c 35 ef 4 ac e a6 3c ad 1e ed ae
  //   e5 16*ff 8a ed 8e 5c 35 ef 4 ac e a6 3c ad 1e ed ae e5 16*ff 8a ed 8e 5c 35 ef a4 ac e a6 3c 24 1e
  //   ed ae e5 16*ff 8a ed 8e 5c 35 ef a4 ac e a6 3c 24 1e 81 2b e5 16*ff 8a ed 8e 5c 35 35 a4 ac e e8 3c
  //   24 1e 81 2b e5 16*ff 8a e8 8e 5c 35 35 a4 ac e e8 3c 24 1e 81 2b fc 16*ff 8a e8 8e 5c 35 35 a4 64 e
  //   e8 3c 24 1e 81 2b fc 16*ff 8a e8 8e 5c 35 35 a4 64 e e8 45 24 3b 81 2b fc 16*ff 8a e8 e7 15 35 35 a4
  //   64 e e8 45 24 3b 81 2b fc 16*ff 8a e8 e7 15 87 35 a4 64 e e8 45 24 3b 81 2b fc 16*ff 8a e8 e7 15 87
  //   35 a4 64 a9 e8 45 24 3b 81 2b fc 16*ff 8a e8 e7 15 87 35 e9 64 a9 e8 45 24 3b 81 91 fc 16*ff 31 e8
  //   e7 15 87 55 e9 64 a9 e8 45 24 3b 81 91 fc 16*ff 31 ff e7 15 87 55 e9 64 a9 e8 45 3b 3b 81 91 fc
  //   16*ff 31 ff e7 15 87 55 e9 64 a9 e8 45 3b 3b 8 91 fc 16*ff 31 ff e7 15 87 55 e9 64 a9 b9 45 3b 4b 8
  //   91 fc 16*ff 31 ff e7 41 87 55 e9 d3 a9 b9 45 3b 4b 8 91 fc 16*ff 31 ff e7 41 87 55 e9 d3 a9 b9 45 3b
  //   4b 8 91 cf 16*ff 31 ff e7 41 87 55 e9 d3 a9 b9 ef 3b 4b 8 91 cf 16*ff 31 ff e7 41 a 55 e9 d3 a9 b9
  //   ef 3b 4b 8 91 cf 16*ff 31 ff 2b 41 a 55 4a d3 a9 b9 ef 3b 4b 8 91 cf 16*ff 31 ff 2b 41 a 55 4a d3 1b
  //   b9 ef 3b 4b 8 91 cf 16*ff 32 ff 2b 41 a 55 4a d3 1b b9 ef 3b 4b 8 a1 cf 16*ff 32 ff 2b 41 a e5 4a d3
  //   1b b9 ef f 4b 8 a1 cf 16*ff 32 22 2b 41 a e5 4a d3 1b b9 ef f 4b 6 a1 cf 16*ff 32 22 2b 41 a e5 4a
  //   d3 1b d6 ef f db 6 a1 cf 16*ff 32 22 2b a a e5 4a e4 1b d6 ef f db 6 a1 cf 16*ff 32 22 2b a a e5 4a
  //   e4 1b d6 ef f db 6 a1 44 16*ff 32 22 2b a 64 e5 4a e4 1b d6 ef f db 6 a1 44 16*ff 32 22 2b a 64 e5
  //   4a e4 10 d6 ef f db 6 a1 44 16*ff 32 22 4e a 64 e5 4a e4 10 d6 ef f db 6 a1 44 16*ff 32 22 4e a 64
  //   e5 65 e4 10 d6 ef 61 db 6 a1 44 16*ff 86 22 4e a 64 e5 65 e4 10 d6 ef 61 db 6 c7 44 16*ff 86 22 4e a
  //   64 36 65 e4 10 d6 ef 61 db 4b c7 44 16*ff 86 70 4e a 64 36 65 68 10 d6 ef 61 db 4b c7 44 16*ff 86 70
  //   4e a 64 36 65 68 10 cd ef 61 69 4b c7 44 16*ff 86 70 4e 8b 64 36 65 68 10 cd ef 61 69 4b c7 44 16*ff
  //   86 70 4e 8b 50 36 65 68 10 cd ef 61 69 4b c7 6d 16*ff 86 70 4e 8b 50 36 65 68 10 cd 6c 61 69 4b c7
  //   6d 16*ff 86 70 4e 8b 50 36 65 68 3e cd 6c 61 69 4b c7 6d 16*ff 86 70 c4 8b 50 36 65 68 3e cd 6c 61
  //   69 4b c7 6d 16*ff 86 70 c4 8b 50 36 26 68 3e cd 6c 61 69 4b b5 6d 16*ff f9 70 c4 8b 50 36 26 68 3e
  //   cd 6c 61 69 4b b5 6d 16*ff f9 70 c4 8b 50 f1 26 68 3e cd 6c 3c 69 4b b5 6d 16*ff f9 b1 c4 8b 50 f1
  //   26 68 3e cd 6c 3c 69 29 b5 6d 16*ff f9 b1 c4 8b 50 f1 26 68 3e a1 6c 3c 85 29 b5 6d 16*ff f9 b1 c4
  //   d1 50 f1 26 4f 3e a1 6c 3c 85 29 b5 6d 16*ff f9 b1 c4 d1 50 f1 26 4f 3e a1 6c 3c 85 29 b5 28 16*ff
  //   f9 b1 c4 d1 de f1 26 4f 3e a1 61 3c 85 29 b5 28 16*ff f9 b1 c4 d1 de f1 78 4f 4e a1 61 3c 85 29 b5
  //   28 16*ff f9 b1 18 d1 de f1 78 4f 4e a1 61 3c 85 29 b5 28 16*ff d8 b1 18 d1 de f1 78 4f 4e a1 61 3c
  //   85 29 70 28 16*ff d8 b1 18 d1 de 6f 78 4f 4e a1 61 3c 85 55 70 28 16*ff d8 b5 18 d1 de 6f 78 4f 4e
  //   a1 61 e 85 55 70 28 16*ff d8 b5 18 d1 de 6f 78 81 4e a1 61 e 85 55 70 28 16*ff d8 b5 18 d1 de 6f 78
  //   81 4e 35 61 e a7 55 70 28 16*ff d8 b5 18 ae de 6f 78 81 4e 35 61 e a7 55 70 1e 16*ff d8 b5 18 ae de
  //   6f 78 81 4e 35 81 e a7 55 70 1e 16*ff d8 b5 18 ae 80 6f 78 81 4e 35 81 e a7 55 70 1e 16*ff d8 b5 18
  //   ae 80 6f 78 81 9a 35 81 e a7 55 70 1e 16*ff d8 b5 80 ae 80 6f 78 81 9a 35 81 e a7 55 70 1e 16*ff 5a
  //   b5 80 ae 80 6f 65 81 9a 35 81 e a7 55 70 1e 16*ff 5a b5 80 ae 80 6f 65 81 9a 35 81 42 a7 55 19 1e
  //   16*ff 5a b5 80 ae 80 4 65 81 9a 35 81 42 a7 31 19 1e 16*ff 5a 7a 80 ae 80 4 65 81 9a 8 81 42 a7 31
  //   19 1e 16*ff 5a 7a 80 ae 80 4 65 c5 9a 8 81 42 6e 31 19 1e 16*ff 5a 7a 80 9b 80 4 65 c5 9a 8 81 42 6e
  //   31 19 8 16*ff 5a 7a 80 9b 80 4 65 c5 9a 8 d5 42 6e 31 19 8 16*ff 5a 7a 80 9b f 4 65 c5 9a 8 d5 42 6e
  //   31 19 8 16*ff 5a 7a 80 9b f 4 65 c5 d8 8 d5 42 6e 31 19 8 16*ff 5a 7a 2d 9b f 4 83 c5 d8 8 d5 42 6e
  //   31 19 8 16*ff f6 7a 2d 9b f 4 83 c5 d8 8 d5 42 6e 31 19 8 16*ff f6 7a 2d 9b f 4 83 c5 d8 8 d5 27 6e
  //   31 2f 8 16*ff f6 a0 2d 9b f bc 83 c5 d8 8 d5 27 6e 31 2f 8 16*ff f6 a0 2d 9b f bc 83 c5 d8 8 d5 27
  //   fa 3b 2f 8 16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
  //   contents of P0806 (hex, n*v repeats v):
  //   7*ff ef ff f7 ee 66 de d5 cd 45 bc 34 2c 23 1b 93 a 7f ff cf b0 b0 cf ff 7f 8*ff f7 ff f9 f2 6c e6
  //   df d9 53 cc 46 40 39 33 ad 26 7f ff cf b0 b0 cf ff 7f 8*ff df b7 b3 af 2b a7 a4 a0 1c 98 14 10 d 9
  //   85 1 7f ff cf b0 b0 cf ff 7f 8*ff bf 80 80 80 0 80 80 80 0 80 4*0 80 0 7f ff cf b0 b0 cf ff 7f 8*ff
  //   fd ff fc f8 75 f2 ef eb 68 e5 62 5e 5b 58 d5 51 7f ff cf b0 b0 cf ff 7f 8*ff fb ff fa f6 71 ed e8 e4
  //   5f db 56 52 4d 49 c4 40 7f ff cf b0 b0 cf ff 7f 8*ff fe ff fd fb 78 f6 f4 f2 70 ee 6b 69 67 65 e3 61
  //   7f ff cf b0 b0 cf ff 7f 10*ff fe fd 7c fb fa fa 79 f8 77 76 75 74 f3 72 7f ff cf b0 b0 cf ff 7f 8*ff
  //   ef 7e 75 ec 63 5a 51 c8 c0 b7 ae a5 1c 93 8a 1 7f ff cf b0 b0 cf ff 7f 8*ff f7 7f 79 f3 6d 67 61 db
  //   d5 cf c9 c3 3d b7 b1 2b 7f ff cf b0 b0 cf ff 7f 8*ff df 37 33 af 2b 27 24 a0 9c 98 94 90 d 89 85 1
  //   7f ff cf b0 b0 cf ff 7f 8*ff bf 0 0 80 0 0 0 5*80 0 80 80 0 7f ff cf b0 b0 cf ff 7f 8*ff fd 7f 7b f7
  //   73 70 6c e8 e4 e1 dd d9 55 d1 ce 4a 7f ff cf b0 b0 cf ff 7f 8*ff fb 7f 7a f5 70 6b 66 e2 dd d8 d3 ce
  //   49 c4 bf 3b 7f ff cf b0 b0 cf ff 7f 8*ff fe 7f 7c f9 76 73 70 ec e9 e6 e3 e0 5d da d7 54 7f ff cf b0
  //   b0 cf ff 7f 9*ff 7f 7d fb 79 78 76 f4 f2 f1 ef ed 6b e9 e8 66 7f ff cf b0 b0 cf ff 7f 8*ff ef fe f5
  //   6c e3 5a 51 48 40 37 ae a5 9c 13 8a 81 7f ff cf b0 b0 cf ff 7f 8*ff f7 ff f9 72 ec 66 5f 59 53 4c c6
  //   c0 b9 33 ad a6 7f ff cf b0 b0 cf ff 7f 8*ff df b2 ae 2b a7 24 20 1d 19 16 92 8f 8b 8 84 81 7f ff cf
  //   b0 b0 cf ff 7f 8*ff bf 80 80 0 80 5*0 80 80 80 0 80 80 7f ff cf b0 b0 cf ff 7f 8*ff fd ff fb 78 f4
  //   70 6d 69 66 62 de db d7 54 d0 cc 7f ff cf b0 b0 cf ff 7f 8*ff fb ff fa 76 f1 6d 68 64 5f 5b d6 d2 cd
  //   49 c4 c0 7f ff cf b0 b0 cf ff 7f 8*ff fe ff fc 79 f7 74 71 6f 6c 69 e7 e4 e1 5e dc d9 7f ff cf b0 b0
  //   cf ff 7f 10*ff fd 7b f9 77 75 73 71 6f ed eb e9 67 e5 e3 7f ff cf b0 b0 cf ff 7f 8*ff ef 65 5d 56 4f
  //   48 41 3a b3 2c a5 1d 16 8f 8 1 7f ff cf b0 b0 cf ff 7f 8*ff f7 7f 78 70 69 62 5b 53 cc 45 be 36 2f
  //   a8 21 1a 7f ff cf b0 b0 cf ff 7f 8*ff df 32 2e 2b 27 24 20 1d 99 16 92 f b 88 4 1 7f ff cf b0 b0 cf
  //   ff 7f 8*ff bf 7*0 80 0 80 0 0 80 0 0 7f ff cf b0 b0 cf ff 7f 8*ff fd 7f 7a 75 71 6c 67 63 de 59 d5
  //   50 4b c6 42 3d 7f ff cf b0 b0 cf ff 7f 8*ff fb 7f 79 74 6e 68 63 5d d8 52 cc 47 41 bc 36 30 7f ff cf
  //   b0 b0 cf ff 7f 8*ff fe 7f 7b 77 73 70 6c 68 e4 61 dd 59 55 d1 4e 4a 7f ff cf b0 b0 cf ff 7f 9*ff 7f
  //   7c 78 75 72 6f 6b e8 65 e2 5e 5b d8 55 51 7f ff cf b0 b0 cf ff 7f 8*ff ef ff 77 6f 67 df d7 4f c7 3f
  //   37 af a7 1f 97 f 7f ff cf b0 b0 cf ff 7f 8*ff f7 ff 79 73 6e e8 e2 5c d6 51 4b c5 bf 39 b4 2e 7f ff
  //   cf b0 b0 cf ff 7f 8*ff df d3 4d 47 41 bb b6 30 aa 24 1e 98 93 d 87 1 7f ff cf b0 b0 cf ff 7f 8*ff bf
  //   80 0 0 0 80 80 0 80 0 0 80 80 0 80 0 7f ff cf b0 b0 cf ff 7f 8*ff fd ff 7c 79 76 f3 f0 6e eb 68 65
  //   e2 df 5c d9 56 7f ff cf b0 b0 cf ff 7f 8*ff fb ff 7b 77 72 ee ea 66 e2 5e 59 d5 d1 4d c9 45 7f ff cf
  //   b0 b0 cf ff 7f 8*ff fe ff 7d 7b 79 f8 f6 74 f2 71 6f ed eb 69 e8 66 7f ff cf b0 b0 cf ff 7f 10*ff 7e
  //   7d 7c fb fa 78 f7 76 75 f4 f3 72 f1 70 7f ff cf b0 b0 cf ff 7f 8*ff ef 7f 77 ef e7 df 57 4f 47 3f 37
  //   af a7 9f 97 8f 7f ff cf b0 b0 cf ff 7f 8*ff f7 7f 79 f2 ec e6 5f 59 53 4c 46 c0 b9 b3 ad a6 7f ff cf
  //   b0 b0 cf ff 7f 8*ff df 44 3f ba b5 b1 2c 27 22 1e 19 94 8f 8b 86 81 7f ff cf b0 b0 cf ff 7f 8*ff bf
  //   0 0 80 80 80 5*0 5*80 7f ff cf b0 b0 cf ff 7f 8*ff fd 7f 7b f7 f3 f0 6c 68 64 61 5d d9 d5 d1 ce ca
  //   7f ff cf b0 b0 cf ff 7f 8*ff fb 7f 7a f5 f0 eb 66 61 5b 56 51 cc c7 c2 bd b8 7f ff cf b0 b0 cf ff 7f
  //   8*ff fe 7f 7c fa f7 f5 72 70 6d 6b 68 e6 e3 e1 de dc 7f ff cf b0 b0 cf ff 7f 9*ff 7f 7d fb f9 f8 76
  //   74 72 71 6f ed eb e9 e8 e6 7f ff cf b0 b0 cf ff 7f 8*ff ef ff f7 ef 66 de d6 ce c6 be b6 ad 25 9d 15
  //   8d 7f ff cf b0 b0 cf ff 7f 8*ff f7 ff f9 f2 6c e6 df d9 d3 cc c6 c0 39 b3 2d a6 7f ff cf b0 b0 cf ff
  //   7f 8*ff df d0 cb c5 3f ba b4 ae a9 a3 9d 98 12 8c 7 81 7f ff cf b0 b0 cf ff 7f 8*ff bf 80 80 80 0
  //   7*80 0 80 0 80 7f ff cf b0 b0 cf ff 7f 8*ff fd ff fc f8 75 f2 ef eb e8 e5 e2 de 5b d8 55 d1 7f ff cf
  //   b0 b0 cf ff 7f 8*ff fb ff fa f5 71 ec e7 e3 de d9 d5 d0 4b c6 42 bd 7f ff cf b0 b0 cf ff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
  //   contents of P0805 (hex, n*v repeats v):
  //   ff c0 80 40 0 3f 7f bf fe c1 81 41 1 3e 7e be fd c2 82 42 2 3d 7d bd fc c3 83 43 3 3c 7c bc fb c4 84
  //   44 4 3b 7b bb fa c5 85 45 5 3a 7a ba f9 c6 86 46 6 39 79 b9 f8 c7 87 47 7 38 78 b8 f7 c8 88 48 8 37
  //   77 b7 f6 c9 89 49 9 36 76 b6 f5 ca 8a 4a a 35 75 b5 f4 cb 8b 4b b 34 74 b4 f3 cc 8c 4c c 33 73 b3 f2
  //   cd 8d 4d d 32 72 b2 f1 ce 8e 4e e 31 71 b1 f0 cf 8f 4f f 30 70 b0 ef d0 90 50 10 2f 6f af ee d1 91
  //   51 11 2e 6e ae ed d2 92 52 12 2d 6d ad ec d3 93 53 13 2c 6c ac eb d4 94 54 14 2b 6b ab ea d5 95 55
  //   15 2a 6a aa e9 d6 96 56 16 29 69 a9 e8 d7 97 57 17 28 68 a8 e7 d8 98 58 18 27 67 a7 e6 d9 99 59 19
  //   26 66 a6 e5 da 9a 5a 1a 25 65 a5 e4 db 9b 5b 1b 24 64 a4 e3 dc 9c 5c 1c 23 63 a3 e2 dd 9d 5d 1d 22
  //   62 a2 e1 de 9e 5e 1e 21 61 a1 e0 df 9f 5f 1f 20 60 a0 df e0 a0 60 20 1f 5f 9f de e1 a1 61 21 1e 5e
  //   9e dd e2 a2 62 22 1d 5d 9d dc e3 a3 63 23 1c 5c 9c db e4 a4 64 24 1b 5b 9b da e5 a5 65 25 1a 5a 9a
  //   d9 e6 a6 66 26 19 59 99 d8 e7 a7 67 27 18 58 98 d7 e8 a8 68 28 17 57 97 d6 e9 a9 69 29 16 56 96 d5
  //   ea aa 6a 2a 15 55 95 d4 eb ab 6b 2b 14 54 94 d3 ec ac 6c 2c 13 53 93 d2 ed ad 6d 2d 12 52 92 d1 ee
  //   ae 6e 2e 11 51 91 d0 ef af 6f 2f 10 50 90 cf f0 b0 70 30 f 4f 8f ce f1 b1 71 31 e 4e 8e cd f2 b2 72
  //   32 d 4d 8d cc f3 b3 73 33 c 4c 8c cb f4 b4 74 34 b 4b 8b ca f5 b5 75 35 a 4a 8a c9 f6 b6 76 36 9 49
  //   89 c8 f7 b7 77 37 8 48 88 c7 f8 b8 78 38 7 47 87 c6 f9 b9 79 39 6 46 86 c5 fa ba 7a 3a 5 45 85 c4 fb
  //   bb 7b 3b 4 44 84 c3 fc bc 7c 3c 3 43 83 c2 fd bd 7d 3d 2 42 82 c1 fe be 7e 3e 1 41 81 c0 ff bf 7f 3f
  //   0 40 80 bf ff c0 80 40 0 3f 7f be fe c1 81 41 1 3e 7e bd fd c2 82 42 2 3d 7d bc fc c3 83 43 3 3c 7c
  //   bb fb c4 84 44 4 3b 7b ba fa c5 85 45 5 3a 7a b9 f9 c6 86 46 6 39 79 b8 f8 c7 87 47 7 38 78 b7 f7 c8
  //   88 48 8 37 77 b6 f6 c9 89 49 9 36 76 b5 f5 ca 8a 4a a 35 75 b4 f4 cb 8b 4b b 34 74 b3 f3 cc 8c 4c c
  //   33 73 b2 f2 cd 8d 4d d 32 72 b1 f1 ce 8e 4e e 31 71 b0 f0 cf 8f 4f f 30 70 af ef d0 90 50 10 2f 6f
  //   ae ee d1 91 51 11 2e 6e ad ed d2 92 52 12 2d 6d ac ec d3 93 53 13 2c 6c ab eb d4 94 54 14 2b 6b aa
  //   ea d5 95 55 15 2a 6a a9 e9 d6 96 56 16 29 69 a8 e8 d7 97 57 17 28 68 a7 e7 d8 98 58 18 27 67 a6 e6
  //   d9 99 59 19 26 66 a5 e5 da 9a 5a 1a 25 65 a4 e4 db 9b 5b 1b 24 64 a3 e3 dc 9c 5c 1c 23 63 a2 e2 dd
  //   9d 5d 1d 22 62 a1 e1 de 9e 5e 1e 21 61 a0 e0 df 9f 5f 1f 20 60 9f df e0 a0 60 20 1f 5f 9e de e1 a1
  //   61 21 1e 5e 9d dd e2 a2 62 22 1d 5d 9c dc e3 a3 63 23 1c 5c 9b db e4 a4 64 24 1b 5b 9a da e5 a5 65
  //   25 1a 5a 99 d9 e6 a6 66 26 19 59 98 d8 e7 a7 67 27 18 58 97 d7 e8 a8 68 28 17 57 96 d6 e9 a9 69 29
  //   16 56 95 d5 ea aa 6a 2a 15 55 94 d4 eb ab 6b 2b 14 54 93 d3 ec ac 6c 2c 13 53 92 d2 ed ad 6d 2d 12
  //   52 91 d1 ee ae 6e 2e 11 51 90 d0 ef af 6f 2f 10 50 8f cf f0 b0 70 30 f 4f 8e ce f1 b1 71 31 e 4e 8d
  //   cd f2 b2 72 32 d 4d 8c cc f3 b3 73 33 c 4c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
  //   contents of P0808 (hex, n*v repeats v):
  //   16*0 5 0 7 0 9 0 b 0 e 0 10 0 14 0 16 0 17 0 19 0 1c 0 1f 0 21 0 23 0 25 90 6 40 5 f0 3 a0 2 c0 9 80
  //   7 40 5 0 3 19*0 5 0 7 0 9 0 b 0 e 0 10 0 14 0 16 0 17 0 19 0 1c 0 1f 0 21 0 23 0 25 d0 7 80 6 30 5
  //   e0 3 0 b c0 8 80 6 40 4 19*0 5 0 7 0 9 0 b 0 e 0 10 0 14 0 16 0 17 0 19 0 1c 0 1f 0 21 0 23 0 25 50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
endmodule
