// Logisim project stargate323_delayAdder_LogisimEvolution.circ as structural Verilog: 1 circuit, main circuit main
module main (
);

  wire clk_out, counter_5_carry, d_ff_1_q, d_ff_2_qn, d_ff_3_q, d_ff_4_q, d_ff_5_q, d_ff_6_q, d_ff_7_q,
       n7474_1_pin1, n7474_1_pin4, n7474_1_pin5, n7474_1_pin9, n7474_1_pin10, n74283_1_pin7, not_1_out,
       not_2_out, not_3_out, not_4_out, not_5_out, not_6_out, not_7_out, not_8_out, RESET_out;
  wire [0:0] n74283_1_pin13;
  wire [7:0] counter_1_q, counter_3_q, counter_4_q, dipswitch_1_p1, multiplexer_1_out, multiplexer_2_out,
       n74283_2_pin5, n74283_2_pin6, P0807_data, P0808_data, P0810_data, register_1_q, rom_1_data, TIMING_q;
  wire [8:0] n74283_2_pin4;
  wire [12:0] counter_2_q;
  wire [12:6] PDL_p1;

  Clock sysclk ();  // open: out
  Clock #(.highDuration(4), .lowDuration(4)) clk (.out(clk_out));
  Counter TIMING (.up(1'b1), .count(1'b1), .clk(clk_out), .Q(TIMING_q));  // open: clr, load, D, carry
  ROM P0810 (.addr(TIMING_q), .data(P0810_data));
  not not_1 (not_1_out, TIMING_q[1]);
  D_Flip_Flop d_ff_1 (.D(not_1_out), .clk(clk_out), .Q(d_ff_1_q));  // open: Qn, preset, reset
  D_Flip_Flop d_ff_2 (.D(P0810_data[0]), .clk(clk_out), .Qn(d_ff_2_qn));  // open: Q, preset, reset
  D_Flip_Flop d_ff_3 (.D(P0810_data[1]), .clk(clk_out), .Q(d_ff_3_q));  // open: Qn, preset, reset
  D_Flip_Flop d_ff_4 (.D(P0810_data[2]), .clk(clk_out), .Q(d_ff_4_q));  // open: Qn, preset, reset
  D_Flip_Flop d_ff_5 (.D(P0810_data[3]), .clk(clk_out), .Q(d_ff_5_q));  // open: Qn, preset, reset
  D_Flip_Flop d_ff_6 (.D(P0810_data[4]), .clk(clk_out), .Q(d_ff_6_q));  // open: Qn, preset, reset
  D_Flip_Flop d_ff_7 (.D(P0810_data[7]), .clk(clk_out), .Q(d_ff_7_q));  // open: Qn, preset, reset
  not not_2 (not_2_out, d_ff_1_q);
  // Probe on d_ff_2_qn
  Counter counter_1 (
    .clr(d_ff_2_qn), .up(1'b1), .count(1'b1), .clk(not_3_out), .Q(counter_1_q));  // open: load, D, carry
  not not_3 (not_3_out, not_2_out);
  // Probe on d_ff_3_q
  not not_4 (not_4_out, d_ff_3_q);
  // Probe on d_ff_4_q
  // Probe on d_ff_5_q
  // Probe on d_ff_6_q
  // Probe on d_ff_7_q
  // Probe on not_4_out
  Counter #(.max('h1fff), .trigger("falling"), .width(13)) counter_2 (
    .up(1'b1), .count(1'b1), .clk(not_8_out), .Q(counter_2_q));  // open: clr, load, D, carry
  // Probe on d_ff_1_q
  // Probe on counter_1_q[0]
  // Probe on counter_1_q[1]
  // Probe on counter_1_q[2]
  // Probe on counter_1_q[3]
  // Probe on counter_1_q[4]
  // Probe on counter_1_q[5]
  // DipSwitch #(.number(4)) dipswitch_1: pin names not known; wires that end beside it: dipswitch_1_p1[0], dipswitch_1_p1[1], dipswitch_1_p1[2], dipswitch_1_p1[3]
  ROM rom_1 (.addr(dipswitch_1_p1), .data(rom_1_data));
  Button RESET (.out(RESET_out));
  not not_5 (not_5_out, counter_1_q[5]);
  not not_6 (not_6_out, not_5_out);
  // DipSwitch #(.number(4)) PDL: pin names not known; wires that end beside it: PDL_p1[6], PDL_p1[7], PDL_p1[8], PDL_p1[12]
  Counter #(.trigger("falling")) counter_3 (
    .clr(RESET_out), .up(1'b1), .count(1'b1), .clk(counter_4_q[7]), .Q(counter_3_q));  // open: load, D, carry
  Counter #(.trigger("falling")) counter_4 (
    .clr(RESET_out), .up(1'b1), .count(1'b1), .clk(not_6_out), .Q(counter_4_q));  // open: load, D, carry
  // DipSwitch #(.number(3)) PGM: pin names not known; wires that end beside it: dipswitch_1_p1[4], dipswitch_1_p1[5], dipswitch_1_p1[6]
  ROM #(.addrWidth(12)) P0807 (.addr({counter_2_q[12:6], counter_1_q[5:1]}), .data(P0807_data));
  ROM #(.addrWidth(13)) P0808 (
    .addr({PDL_p1[12], dipswitch_1_p1[6:4], PDL_p1[8:6], counter_1_q[5:0]}), .data(P0808_data));
  Counter #(.max('hf), .width(4)) counter_5 (
    .load(counter_5_carry), .up(1'b1), .count(1'b1), .clk(counter_1_q[5]), .D(rom_1_data[3:0]),
    .carry(counter_5_carry));  // open: clr, Q
  // Probe on counter_4_q
  // Probe on TIMING_q
  // Probe on counter_3_q
  // Probe on P0807_data
  Multiplexer #(.enable("false"), .width(8)) multiplexer_1 (
    .in0(counter_4_q), .in1(counter_3_q), .out(multiplexer_1_out), .sel(counter_1_q[0]));
  // Probe on P0808_data
  // Probe on multiplexer_2_out
  Multiplexer #(.enable("false"), .width(8)) multiplexer_2 (
    .in0(P0808_data), .in1(P0807_data), .out(multiplexer_2_out), .sel(not_7_out));
  // Probe on not_7_out
  not not_7 (not_7_out, d_ff_7_q);
  Register register_1 (.D(multiplexer_2_out), .en(1'b1), .clk(d_ff_1_q), .Q(register_1_q));  // open: clr
  // Probe on multiplexer_1_out
  // Probe on register_1_q
  _7474 #(.ShowInternalStructure("true")) u_7474_1 (
    .pin1(n7474_1_pin1), .pin2(counter_5_carry), .pin3(counter_1_q[5]), .pin4(n7474_1_pin4),
    .pin5(n7474_1_pin5), .pin13(d_ff_6_q), .pin12(n74283_2_pin4[8]), .pin11(d_ff_1_q), .pin10(n7474_1_pin10),
    .pin9(n7474_1_pin9));  // open: pin6, pin8
  not not_8 (not_8_out, n7474_1_pin5);
  _74283 #(.ShowInternalStructure("true")) u_74283_1 (
    .pin1(n74283_2_pin4[5]), .pin2(n74283_2_pin6[5]), .pin3(n74283_2_pin5[5]), .pin4(n74283_2_pin4[4]),
    .pin5(n74283_2_pin5[4]), .pin6(n74283_2_pin6[4]), .pin7(n74283_1_pin7), .pin15(n74283_2_pin6[6]),
    .pin14(n74283_2_pin5[6]), .pin13(n74283_1_pin13[0]), .pin12(n74283_2_pin5[7]), .pin11(n74283_2_pin6[7]),
    .pin10(n74283_2_pin4[7]), .pin9(n74283_2_pin4[8]));
  _74283 #(.ShowInternalStructure("true")) u_74283_2 (
    .pin1(n74283_2_pin4[1]), .pin2(n74283_2_pin6[1]), .pin3(n74283_2_pin5[1]), .pin4(n74283_2_pin4[0]),
    .pin5(n74283_2_pin5[0]), .pin6(n74283_2_pin6[0]), .pin7(n7474_1_pin9), .pin15(n74283_2_pin6[2]),
    .pin14(n74283_2_pin5[2]), .pin13(n74283_2_pin4[2]), .pin12(n74283_2_pin5[3]), .pin11(n74283_2_pin6[3]),
    .pin10(n74283_2_pin4[3]), .pin9(n74283_1_pin7));
  // Probe on n74283_2_pin4[8]
  // Probe on {n74283_2_pin4[7], n74283_2_pin4[5:0], n74283_1_pin13[0]}
  // Probe on {n74283_2_pin4[8:7], n74283_2_pin4[7], n74283_2_pin4[5:0]}
  // also tied to GND on the sheet: {n74283_2_pin6[0], n74283_2_pin6[1], n74283_2_pin6[2], n74283_2_pin6[3], n74283_2_pin6[4], n74283_2_pin6[5], n74283_2_pin6[6], n74283_2_pin6[7], n74283_2_pin5[7]}
  // also tied to VCC on the sheet: {n7474_1_pin1, n7474_1_pin4, n7474_1_pin10, n74283_2_pin5[0], n74283_2_pin5[1], n74283_2_pin5[2], n74283_2_pin5[3], n74283_2_pin5[4], n74283_2_pin5[5], n74283_2_pin5[6]}

  // Notes on the sheet:
  //   contents of P0810 (hex, n*v repeats v):
  //   e4 e4 e4 e5 e5 c5 5*e5 c5 4*e5 c5 e5 e5 e5 c5 e5 e5 e5 c5 e5 e5 c5 e5 e5 c5 e5 85 a5 e5 e5 e5 c5 e5
  //   e5 e5 c5 e5 e5 e5 c5 e5 e5 e5 c5 e5 e5 c5 e5 e5 c5 e5 e5 d5 f5 75 55 75 7d fb 9b a3 f3 73 73 7b 7b
  //   ff fb e3 f3 73 73 7b 7b ff fb e3 f3 73 73 7b 7b ff fb e3 f3 73 73 7b 7b ff fb e3 f3 73 73 7b 7b ff
  //   fb e3 f3 73 73 7b 7b ff fb e3 f3 73 73 7b 7b ff fb e3 f3 73 73 7b 7b ff fb e3 f3 73 73 7b 7b ff fb
  //   e3 f3 73 73 7b 7b ff fb e3 f3 73 73 7b 7b ff fb e3 f3 73 73 7b 7b ff fb e3 f3 73 73 7b 7b ff fb e3
  //   f3 73 73 7b 7b ff fb e3 f3 f3 f3 fb fb ff fb e3 f3 f3 f3 fb fb ff fb e3 f3 f3 f3 fb fb ff fb e3 f3
  //   f3 f3 fb fb ff fb e3 f3 f3 f3 fb fb ff fb e3 f3 f3 f3 fb fb ff fb e3 f3 f3 f3 fb fb ff fb e3 f3 f3
  //   f3 fb fb ff fb e3 f3 f3 f3 fb fb ff fb e3 e3 eb e2 c2 e2
  //   contents of rom_1 (hex, n*v repeats v):
  //   eb ea e9 e9 12*e7 eb e9 e7 e7 12*e5 ec eb 14*ea 4*ec 13*ea e8 e6 e6 12*e4 ea e9 e7 e7 12*e4 e9 e7 e5
  //   e5 12*e4 e9 e6 e5 e5 12*e4 eb ea e9 e9 12*e7 eb e9 e7 e7 12*e5 ec eb 14*ea 4*ec 13*ea e8 e6 e6 12*e4
  //   ea e9 e7 e7 12*e4 e9 e7 e5 e5 12*e4 e9 e6 e5 e5 12*e4
  //   contents of P0807 (hex, n*v repeats v):
  //   6*ff 2e ed a9 5c 35 ef 4 ac 72 a6 3c ad 1e ed ae e5 16*ff 2e ed 8e 5c 35 ef 4 ac e a6 3c ad 1e ed ae
  //   e5 16*ff 8a ed 8e 5c 35 ef 4 ac e a6 3c ad 1e ed ae e5 16*ff 8a ed 8e 5c 35 ef a4 ac e a6 3c 24 1e
  //   ed ae e5 16*ff 8a ed 8e 5c 35 ef a4 ac e a6 3c 24 1e 81 2b e5 16*ff 8a ed 8e 5c 35 35 a4 ac e e8 3c
  //   24 1e 81 2b e5 16*ff 8a e8 8e 5c 35 35 a4 ac e e8 3c 24 1e 81 2b fc 16*ff 8a e8 8e 5c 35 35 a4 64 e
  //   e8 3c 24 1e 81 2b fc 16*ff 8a e8 8e 5c 35 35 a4 64 e e8 45 24 3b 81 2b fc 16*ff 8a e8 e7 15 35 35 a4
  //   64 e e8 45 24 3b 81 2b fc 16*ff 8a e8 e7 15 87 35 a4 64 e e8 45 24 3b 81 2b fc 16*ff 8a e8 e7 15 87
  //   35 a4 64 a9 e8 45 24 3b 81 2b fc 16*ff 8a e8 e7 15 87 35 e9 64 a9 e8 45 24 3b 81 91 fc 16*ff 31 e8
  //   e7 15 87 55 e9 64 a9 e8 45 24 3b 81 91 fc 16*ff 31 ff e7 15 87 55 e9 64 a9 e8 45 3b 3b 81 91 fc
  //   16*ff 31 ff e7 15 87 55 e9 64 a9 e8 45 3b 3b 8 91 fc 16*ff 31 ff e7 15 87 55 e9 64 a9 b9 45 3b 4b 8
  //   91 fc 16*ff 31 ff e7 41 87 55 e9 d3 a9 b9 45 3b 4b 8 91 fc 16*ff 31 ff e7 41 87 55 e9 d3 a9 b9 45 3b
  //   4b 8 91 cf 16*ff 31 ff e7 41 87 55 e9 d3 a9 b9 ef 3b 4b 8 91 cf 16*ff 31 ff e7 41 a 55 e9 d3 a9 b9
  //   ef 3b 4b 8 91 cf 16*ff 31 ff 2b 41 a 55 4a d3 a9 b9 ef 3b 4b 8 91 cf 16*ff 31 ff 2b 41 a 55 4a d3 1b
  //   b9 ef 3b 4b 8 91 cf 16*ff 32 ff 2b 41 a 55 4a d3 1b b9 ef 3b 4b 8 a1 cf 16*ff 32 ff 2b 41 a e5 4a d3
  //   1b b9 ef f 4b 8 a1 cf 16*ff 32 22 2b 41 a e5 4a d3 1b b9 ef f 4b 6 a1 cf 16*ff 32 22 2b 41 a e5 4a
  //   d3 1b d6 ef f db 6 a1 cf 16*ff 32 22 2b a a e5 4a e4 1b d6 ef f db 6 a1 cf 16*ff 32 22 2b a a e5 4a
  //   e4 1b d6 ef f db 6 a1 44 16*ff 32 22 2b a 64 e5 4a e4 1b d6 ef f db 6 a1 44 16*ff 32 22 2b a 64 e5
  //   4a e4 10 d6 ef f db 6 a1 44 16*ff 32 22 4e a 64 e5 4a e4 10 d6 ef f db 6 a1 44 16*ff 32 22 4e a 64
  //   e5 65 e4 10 d6 ef 61 db 6 a1 44 16*ff 86 22 4e a 64 e5 65 e4 10 d6 ef 61 db 6 c7 44 16*ff 86 22 4e a
  //   64 36 65 e4 10 d6 ef 61 db 4b c7 44 16*ff 86 70 4e a 64 36 65 68 10 d6 ef 61 db 4b c7 44 16*ff 86 70
  //   4e a 64 36 65 68 10 cd ef 61 69 4b c7 44 16*ff 86 70 4e 8b 64 36 65 68 10 cd ef 61 69 4b c7 44 16*ff
  //   86 70 4e 8b 50 36 65 68 10 cd ef 61 69 4b c7 6d 16*ff 86 70 4e 8b 50 36 65 68 10 cd 6c 61 69 4b c7
  //   6d 16*ff 86 70 4e 8b 50 36 65 68 3e cd 6c 61 69 4b c7 6d 16*ff 86 70 c4 8b 50 36 65 68 3e cd 6c 61
  //   69 4b c7 6d 16*ff 86 70 c4 8b 50 36 26 68 3e cd 6c 61 69 4b b5 6d 16*ff f9 70 c4 8b 50 36 26 68 3e
  //   cd 6c 61 69 4b b5 6d 16*ff f9 70 c4 8b 50 f1 26 68 3e cd 6c 3c 69 4b b5 6d 16*ff f9 b1 c4 8b 50 f1
  //   26 68 3e cd 6c 3c 69 29 b5 6d 16*ff f9 b1 c4 8b 50 f1 26 68 3e a1 6c 3c 85 29 b5 6d 16*ff f9 b1 c4
  //   d1 50 f1 26 4f 3e a1 6c 3c 85 29 b5 6d 16*ff f9 b1 c4 d1 50 f1 26 4f 3e a1 6c 3c 85 29 b5 28 16*ff
  //   f9 b1 c4 d1 de f1 26 4f 3e a1 61 3c 85 29 b5 28 16*ff f9 b1 c4 d1 de f1 78 4f 4e a1 61 3c 85 29 b5
  //   28 16*ff f9 b1 18 d1 de f1 78 4f 4e a1 61 3c 85 29 b5 28 16*ff d8 b1 18 d1 de f1 78 4f 4e a1 61 3c
  //   85 29 70 28 16*ff d8 b1 18 d1 de 6f 78 4f 4e a1 61 3c 85 55 70 28 16*ff d8 b5 18 d1 de 6f 78 4f 4e
  //   a1 61 e 85 55 70 28 16*ff d8 b5 18 d1 de 6f 78 81 4e a1 61 e 85 55 70 28 16*ff d8 b5 18 d1 de 6f 78
  //   81 4e 35 61 e a7 55 70 28 16*ff d8 b5 18 ae de 6f 78 81 4e 35 61 e a7 55 70 1e 16*ff d8 b5 18 ae de
  //   6f 78 81 4e 35 81 e a7 55 70 1e 16*ff d8 b5 18 ae 80 6f 78 81 4e 35 81 e a7 55 70 1e 16*ff d8 b5 18
  //   ae 80 6f 78 81 9a 35 81 e a7 55 70 1e 16*ff d8 b5 80 ae 80 6f 78 81 9a 35 81 e a7 55 70 1e 16*ff 5a
  //   b5 80 ae 80 6f 65 81 9a 35 81 e a7 55 70 1e 16*ff 5a b5 80 ae 80 6f 65 81 9a 35 81 42 a7 55 19 1e
  //   16*ff 5a b5 80 ae 80 4 65 81 9a 35 81 42 a7 31 19 1e 16*ff 5a 7a 80 ae 80 4 65 81 9a 8 81 42 a7 31
  //   19 1e 16*ff 5a 7a 80 ae 80 4 65 c5 9a 8 81 42 6e 31 19 1e 16*ff 5a 7a 80 9b 80 4 65 c5 9a 8 81 42 6e
  //   31 19 8 16*ff 5a 7a 80 9b 80 4 65 c5 9a 8 d5 42 6e 31 19 8 16*ff 5a 7a 80 9b f 4 65 c5 9a 8 d5 42 6e
  //   31 19 8 16*ff 5a 7a 80 9b f 4 65 c5 d8 8 d5 42 6e 31 19 8 16*ff 5a 7a 2d 9b f 4 83 c5 d8 8 d5 42 6e
  //   31 19 8 16*ff f6 7a 2d 9b f 4 83 c5 d8 8 d5 42 6e 31 19 8 16*ff f6 7a 2d 9b f 4 83 c5 d8 8 d5 27 6e
  //   31 2f 8 16*ff f6 a0 2d 9b f bc 83 c5 d8 8 d5 27 6e 31 2f 8 16*ff f6 a0 2d 9b f bc 83 c5 d8 8 d5 27
  //   fa 3b 2f 8 16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
  //   contents of P0808 (hex, n*v repeats v):
  //   16*0 5 0 7 0 9 0 b 0 e 0 10 0 14 0 16 0 17 0 19 0 1c 0 1f 0 21 0 23 0 25 90 6 40 5 f0 3 a0 2 c0 9 80
  //   7 40 5 0 3 19*0 5 0 7 0 9 0 b 0 e 0 10 0 14 0 16 0 17 0 19 0 1c 0 1f 0 21 0 23 0 25 d0 7 80 6 30 5
  //   e0 3 0 b c0 8 80 6 40 4 19*0 5 0 7 0 9 0 b 0 e 0 10 0 14 0 16 0 17 0 19 0 1c 0 1f 0 21 0 23 0 25 50
  //   5 0 4 b0 2 60 1 80 8 40 6 0 4 c0 1 19*0 5 0 7 0 9 0 b 0 e 0 10 0 14 0 16 0 17 0 19 0 1c 0 1f 0 21 0
  //   23 0 25 10 4 c0 2 70 1 20 0 40 7 0 5 c0 2 80 20*0 5 0 7 0 9 0 b 0 e 0 10 0 14 0 16 0 17 0 19 0 1c 0
  //   1f 0 21 0 23 0 25 50 a 0 9 b0 7 60 6 80 d 40 b 0 9 c0 6 19*0 5 0 7 0 9 0 b 0 e 0 10 0 14 0 16 0 17 0
  //   19 0 1c 0 1f 0 21 0 23 0 25 10 9 c0 7 70 6 20 5 40 c 0 a c0 7 80 5 19*0 5 0 7 0 9 0 b 0 e 0 10 0 14
  //   0 16 0 17 0 19 0 1c 0 1f 0 21 0 23 0 25 90 b 40 a f0 8 a0 7 c0 e 80 c 40 a 0 8 19*0 5 0 7 0 9 0 b 0
  //   e 0 10 0 14 0 16 0 17 0 19 0 1c 0 1f 0 21 0 23 0 25 10 e c0 c 70 b 20 a 40 11 0 f c0 c 80 a 19*0 8 0
  //   a 0 b 0 10 0 11 0 15 0 16 0 19 0 1c 0 1f 0 22 0 24 0 27 0 2a 0 2c e0 7 20 6 60 4 a0 2 20 c 20 9 20 6
  //   20 3 19*0 8 0 a 0 b 0 10 0 11 0 15 0 16 0 19 0 1c 0 1f 0 22 0 24 0 27 0 2a 0 2c 20 9 60 7 a0 5 e0 3
  //   60 d 60 a 60 7 60 4 19*0 8 0 a 0 b 0 10 0 11 0 15 0 16 0 19 0 1c 0 1f 0 22 0 24 0 27 0 2a 0 2c a0 6
  //   e0 4 20 3 60 1 e0 a e0 7 e0 4 e0 1 19*0 8 0 a 0 b 0 10 0 11 0 15 0 16 0 19 0 1c 0 1f 0 22 0 24 0 27
  //   0 2a 0 2c 60 5 a0 3 e0 1 20 0 a0 9 a0 6 a0 3 a0 20*0 8 0 a 0 b 0 10 0 11 0 15 0 16 0 19 0 1c 0 1f 0
  //   22 0 24 0 27 0 2a 0 2c a0 b e0 9 20 8 60 6 e0 f e0 c e0 9 e0 6 19*0 8 0 a 0 b 0 10 0 11 0 15 0 16 0
  //   19 0 1c 0 1f 0 22 0 24 0 27 0 2a 0 2c 60 a a0 8 e0 6 20 5 a0 e a0 b a0 8 a0 5 19*0 8 0 a 0 b 0 10 0
  //   11 0 15 0 16 0 19 0 1c 0 1f 0 22 0 24 0 27 0 2a 0 2c e0 c 20 b 60 9 a0 7 20 11 20 e 20 b 20 8 19*0 8
  //   0 a 0 b 0 10 0 11 0 15 0 16 0 19 0 1c 0 1f 0 22 0 24 0 27 0 2a 0 2c 60 f a0 d e0 b 20 a a0 13 a0 10
  //   a0 d a0 a 19*0 3 0 5 0 6 0 8 0 b 0 c 0 e 0 11 0 12 0 14 0 17 0 18 0 19 0 1d 0 1e 40 5 60 4 80 3 a0 2
  //   60 7 e0 5 60 4 e0 2 19*0 3 0 5 0 6 0 8 0 b 0 c 0 e 0 11 0 12 0 14 0 17 0 18 0 19 0 1d 0 1e 80 6 a0 5
  //   c0 4 e0 3 a0 8 20 7 a0 5 20 4 19*0 3 0 5 0 6 0 8 0 b 0 c 0 e 0 11 0 12 0 14 0 17 0 18 0 19 0 1d 0 1e
  //   0 4 20 3 40 2 60 1 20 6 a0 4 20 3 a0 1 19*0 3 0 5 0 6 0 8 0 b 0 c 0 e 0 11 0 12 0 14 0 17 0 18 0 19
  //   0 1d 0 1e c0 2 e0 1 0 1 20 0 e0 4 60 3 e0 1 60 20*0 3 0 5 0 6 0 8 0 b 0 c 0 e 0 11 0 12 0 14 0 17 0
  //   18 0 19 0 1d 0 1e 0 9 20 8 40 7 60 6 20 b a0 9 20 8 a0 6 19*0 3 0 5 0 6 0 8 0 b 0 c 0 e 0 11 0 12 0
  //   14 0 17 0 18 0 19 0 1d 0 1e c0 7 e0 6 0 6 20 5 e0 9 60 8 e0 6 60 5 19*0 3 0 5 0 6 0 8 0 b 0 c 0 e 0
  //   11 0 12 0 14 0 17 0 18 0 19 0 1d 0 1e 40 a 60 9 80 8 a0 7 60 c e0 a 60 9 e0 7 19*0 3 0 5 0 6 0 8 0 b
  //   0 c 0 e 0 11 0 12 0 14 0 17 0 18 0 19 0 1d 0 1e c0 c e0 b 0 b 20 a e0 e 60 d e0 b 60 a 19*0 2 0 4 0
  //   5 0 7 0 8 0 9 0 b 0 d 0 e 0 f 0 10 0 12 0 14 0 15 0 16 f0 3 80 3 10 3 a0 2 0 5 40 4 80 3 c0 2 19*0 2
  //   0 4 0 5 0 7 0 8 0 9 0 b 0 d 0 e 0 f 0 10 0 12 0 14 0 15 0 16 30 5 c0 4 50 4 e0 3 40 6 80 5 c0 4 0 4
  //   19*0 2 0 4 0 5 0 7 0 8 0 9 0 b 0 d 0 e 0 f 0 10 0 12 0 14 0 15 0 16 b0 2 40 2 d0 1 60 1 c0 3 0 3 40
  //   2 80 1 19*0 2 0 4 0 5 0 7 0 8 0 9 0 b 0 d 0 e 0 f 0 10 0 12 0 14 0 15 0 16 70 1 0 1 90 0 20 0 80 2
  //   c0 1 0 1 40 20*0 2 0 4 0 5 0 7 0 8 0 9 0 b 0 d 0 e 0 f 0 10 0 12 0 14 0 15 0 16 b0 7 40 7 d0 6 60 6
  //   c0 8 0 8 40 7 80 6 19*0 2 0 4 0 5 0 7 0 8 0 9 0 b 0 d 0 e 0 f 0 10 0 12 0 14 0 15 0 16 70 6 0 6 90 5
  //   20 5 80 7 c0 6 0 6 40 5 19*0 2 0 4 0 5 0 7 0 8 0 9 0 b 0 d 0 e 0 f 0 10 0 12 0 14 0 15 0 16 f0 8 80
  //   8 10 8 a0 7 0 a 40 9 80 8 c0 7 19*0 2 0 4 0 5 0 7 0 8 0 9 0 b 0 d 0 e 0 f 0 10 0 12 0 14 0 15 0 16
  //   70 b 0 b 90 a 20 a 80 c c0 b 0 b 40 a 19*0 f 0 10 0 11 0 14 0 15 0 19 0 1c 0 20 0 24 0 28 0 2c 0 2f
  //   0 34 0 3b 0 3f 80 a e0 7 40 5 a0 2 e0 10 60 c e0 7 60 3 19*0 f 0 10 0 11 0 14 0 15 0 19 0 1c 0 20 0
  //   24 0 28 0 2c 0 2f 0 34 0 3b 0 3f c0 b 20 9 80 6 e0 3 20 12 a0 d 20 9 a0 4 19*0 f 0 10 0 11 0 14 0 15
  //   0 19 0 1c 0 20 0 24 0 28 0 2c 0 2f 0 34 0 3b 0 3f 40 9 a0 6 0 4 60 1 a0 f 20 b a0 6 20 2 19*0 f 0 10
  //   0 11 0 14 0 15 0 19 0 1c 0 20 0 24 0 28 0 2c 0 2f 0 34 0 3b 0 3f 0 8 60 5 c0 2 20 0 60 e e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
endmodule
